# Fritzing sketch Robot Arm + Camera Wiring (saved by Fritzing 1.0.2b)

parts:
  Part1 = Adafruit PCA9685 PWM/Servo Breakout [part_number=815]
  JACK1 = 2.1mm Barrel Jack with Terminal Block  # not connected
  Part2 = Arduino Uno (Rev3) - ICSP
  J4 = Basic Servo
  J5 = Basic Servo
  A1 = Arducam mini 2mp plus pins swapped
  J6 = Basic Servo
  J7 = Basic Servo
  J8 = Basic Servo

nets:
  N1: Part1.PWM4, J8.pulse
  VCC: Part1.5.0V, Part2.VIN, J4.vcc, J5.vcc, J6.vcc, J7.vcc, J8.vcc
  GND: Part1.GND, Part2.GND, J4.gnd, J5.gnd, A1.Pin_4, J6.gnd, J7.gnd, J8.gnd
  N2: Part1.PWM3, J7.pulse
  N3: Part1.PWM2, J6.pulse
  N4: Part1.PWM1, J4.pulse
  N5: Part1.PWM0, J5.pulse
  VCC_2: Part1.VCC, Part2.5V, A1.Pin_3
  N6: Part1.SDA, Part2.A4/SDA, A1.Pin_2
  N7: Part1.SCL, Part2.A5/SCL, A1.Pin_1
  N8: Part2.ICSP_MISO, A1.Pin_6
  N9: Part2.ICSP_SCK, A1.Pin_5
  N10: Part2.ICSP_MOSI, Part2.D11_PWM/MOSI, A1.Pin_7
  N11: Part2.D10_PWM/SS, A1.Pin_8

notes:
  BASE (0) GRIPPER (1) WRIST (2) ELBOW (3) SHOULDER (4)
  CS MOSI MISO SCK GND VCC SDA SCL
  CS - Pin 10
  MOSI - Pin 11
  MISO - Pin 12
  SCK - Pin 13
  GND - GND
  VCC - VCC
  SDA - Pin A4
  SCL - Pin A5

custom parts:
  Adafruit PCA9685 PWM/Servo Breakout: Using only two pins, control 16 free-running PWM outputs! I2C-controlled PWM driver with a built in clock. Unlike the TLC5940 family, you do not need to continuously send it signal tying up your microcontroller, its completely free running! 5V compliant, which means you can control it from a 3.3V microcontroller and still safely drive up to 6V outputs (this is good for when you want to control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
  Arducam mini 2mp plus pins swapped: ArduCAM-2MP-Plus is a high-definition 2MP SPI camera, which reduces the complexity of the camera control interface.This version is from the back of the board.
